// Logisim project LC-2200-16.circ as structural Verilog: 1 circuit, main circuit main
module main (
);

  wire ALUHi, ALULo, chkZ, CLK, comparator_1_eq, comparator_2_eq, DrALU, DrMEM, DrOFF, DrPC, DrREG, LdA, LdB,
       LdIR, LdMAR, LdPC, LdZ, not_1_out, OPTest, RegSelHi, RegSelLo, WrMEM, WrREG, Z;
  wire [1:0] bit_extender_1_out;
  wire [2:0] OP;
  wire [3:0] regno, RX, RY, RZ;
  wire [4:4] IR_q;
  wire [5:0] multiplexer_1_out, Next_State_q, ONZ_ROM, OP_ROM, State;
  wire [15:0] A_q, adder_1_out, adder_2_out, and_1_out, B_q, bit_extender_2_out, bit_extender_3_out,
       controlled_buffer_1_out, MAR_q, multiplexer_2_out, nand_1_out, PC_q, ram_1_data, ram_2_data,
       subtractor_1_out;

  assign bit_extender_1_out = {{1{1'b0}}, Z};  // Bit_Extender bit_extender_1
  Register #(.width(16)) PC (.D(controlled_buffer_1_out), .en(LdPC), .Q(PC_q), .clk(CLK));  // open: clr
  assign controlled_buffer_1_out = DrPC ? PC_q : 16'bz;  // Controlled_Buffer controlled_buffer_1
  Multiplexer #(.select(2), .width(6)) multiplexer_1 (
    .in0(State), .in1(OP_ROM), .in2(ONZ_ROM), .out(multiplexer_1_out), .sel({chkZ, OPTest}), .en(1'b1));  // open: in3
  ROM #(.addrWidth(3), .dataWidth(6)) rom_1 (.addr(OP), .data(OP_ROM));  // open: sel
  ROM #(.addrWidth(2), .dataWidth(6)) rom_2 (.addr(bit_extender_1_out), .data(ONZ_ROM));  // open: sel
  Register #(.width(6)) Next_State (.D(multiplexer_1_out), .Q(Next_State_q), .clk(CLK));  // open: en, clr
  Clock clock_1 (.out(CLK));
  Register #(.width(16)) A (.D(controlled_buffer_1_out), .en(LdA), .Q(A_q), .clk(CLK));  // open: clr
  Adder #(.width(16)) adder_1 (.a(A_q), .b(B_q), .out(adder_1_out));  // open: cin, cout
  assign nand_1_out = ~(B_q & A_q);  // NAND_Gate nand_1, 16 bits wide
  Register #(.width(16)) B (.D(controlled_buffer_1_out), .en(LdB), .Q(B_q), .clk(CLK));  // open: clr
  Subtractor #(.width(16)) subtractor_1 (.a(A_q), .b(B_q), .out(subtractor_1_out));  // open: bin, bout
  Adder #(.width(16)) adder_2 (.a(A_q), .b(16'h1), .out(adder_2_out));  // open: cin, cout
  Multiplexer #(.select(2), .width(16)) multiplexer_2 (
    .in0(adder_1_out), .in1(nand_1_out), .in2(subtractor_1_out), .in3(adder_2_out), .out(multiplexer_2_out),
    .sel({ALUHi, ALULo}));  // open: en
  assign controlled_buffer_1_out = DrALU ? multiplexer_2_out : 16'bz;  // Controlled_Buffer controlled_buffer_2
  ROM #(.addrWidth(6), .dataWidth(25)) rom_3 (
    .addr(Next_State_q),
    .data({chkZ, OPTest, ALUHi, ALULo, RegSelHi, RegSelLo, WrMEM, WrREG, LdZ, LdB, LdA, LdMAR, LdIR, LdPC, DrOFF, DrPC, DrALU, DrMEM, DrREG, State}));  // open: sel
  Comparator #(.width(16)) comparator_1 (
    .a(controlled_buffer_1_out), .b({16{1'b0}}), .eq(comparator_1_eq));  // open: gt, lt
  Multiplexer #(.select(2), .width(4)) multiplexer_3 (
    .in0(RX), .in1(RY), .in2(RZ), .out(regno), .sel({RegSelHi, RegSelLo}), .en(1'b1));  // open: in3
  not not_1 (not_1_out, comparator_2_eq);
  Comparator #(.width(4)) comparator_2 (.a(regno), .b(4'b0000), .eq(comparator_2_eq));  // open: gt, lt
  Register #(.width(1)) u_Z (.D(comparator_1_eq), .en(LdZ), .Q(Z), .clk(CLK));  // open: clr
  RAM #(.addrWidth(4), .dataWidth(16), .bus("separate")) ram_1 (
    .addr(regno), .din(controlled_buffer_1_out), .data(ram_1_data), .str(WrREG), .clk(CLK), .ld(1'b1));  // open: sel, clr
  assign bit_extender_2_out = {{15{not_1_out}}, not_1_out};  // Bit_Extender bit_extender_2
  assign and_1_out = bit_extender_2_out & ram_1_data;  // AND_Gate and_1, 16 bits wide
  assign controlled_buffer_1_out = DrREG ? and_1_out : 16'bz;  // Controlled_Buffer controlled_buffer_3
  Register #(.width(16)) MAR (.D(controlled_buffer_1_out), .en(LdMAR), .Q(MAR_q), .clk(CLK));  // open: clr
  RAM #(.addrWidth(16), .dataWidth(16), .bus("separate")) ram_2 (
    .addr(MAR_q), .din(controlled_buffer_1_out), .data(ram_2_data), .str(WrMEM), .sel(CLK), .clk(1'b1));  // open: ld, clr
  assign controlled_buffer_1_out = DrMEM ? ram_2_data : 16'bz;  // Controlled_Buffer controlled_buffer_4
  Register #(.width(16)) IR (
    .D(controlled_buffer_1_out), .en(LdIR), .Q({OP, RX, RY, IR_q[4], RZ}), .clk(CLK));  // open: clr
  assign bit_extender_3_out = {{11{IR_q[4]}}, {IR_q[4], RZ}};  // Bit_Extender bit_extender_3
  assign controlled_buffer_1_out = DrOFF ? bit_extender_3_out : 16'bz;  // Controlled_Buffer controlled_buffer_5

  // Notes on the sheet:
  //   OP ROM
  //   ONZ ROM
  //   LC-2200 Datapath
  //   main ROM
  //   register file 16*16
  //   Memory 65536*16 bit
endmodule
